# Fritzing sketch schemactic (saved by Fritzing 1.0.2b)
breadboards: 1

parts:
  Part1 = Arduino Uno (Rev3) - ICSP
  LED1 = LED - 5mm [color="Red (633nm)" current=0.030A package="5 mm [THT]"]
  R1 = Resistor [tolerance=±5% resistance=220 package="0402 [SMD]"]
  A1 = MH-FMD buzzer

nets:
  N1: Part1.D8, A1.Pin_2
  N2: Part1.GND, R1.Pin_0, A1.Pin_3
  N3: Part1.D7, LED1.anode
  N4: Part1.5V, A1.Pin_1
  N5: LED1.cathode, R1.Pin_1

custom parts:
  MH-FMD buzzer: MH-FMD buzzer.
